# Fritzing sketch SCARA (saved by Fritzing 0.9.0b)
circuit board: 11.1613cm x 8.041cm
breadboards: 1

parts:
  Part2 = Arduino Uno (Rev3)
  U2 = MAX485 [package=dil08]
  R3 = Resistor [tolerance=±5% resistance=220 package=THT]
  CUP_TXD1 = female pin header, 2 pins [form="♀ (female)"]
  dynamixel1 = female pin header, 2 pins [form="♀ (female)"]
  J4 = female pin header, 2 pins [form="♀ (female)"]
  12V1 = Power plug
  Q3 = NPN-Transistor [package="TO92 [THT]"]
  C2 = Electrolytic Capacitor [capacitance=1µF package="100 mil [THT, electrolytic]"]
  R4 = Resistor [tolerance=±5% resistance=220 package=THT]
  J5 = female pin header, 2 pins [form="♀ (female)"]
  J6 = female pin header, 2 pins [form="♀ (female)"]
  J7 = female pin header, 2 pins [form="♀ (female)"]
  J8 = female pin header, 2 pins [form="♀ (female)"]  # not connected
  J9 = female pin header, 2 pins [form="♀ (female)"]  # not connected
  J10 = female pin header, 2 pins [form="♀ (female)"]
  J11 = female pin header, 2 pins [form="♀ (female)"]
  J12 = female pin header, 2 pins [form="♀ (female)"]
  J13 = female pin header, 2 pins [form="♀ (female)"]
  J14 = female pin header, 2 pins [form="♀ (female)"]
  J15 = female pin header, 2 pins [form="♀ (female)"]
  J16 = female pin header, 2 pins [form="♀ (female)"]
  J17 = female pin header, 2 pins [form="♀ (female)"]
  J18 = female pin header, 2 pins [form="♀ (female)"]
  J19 = female pin header, 2 pins [form="♀ (female)"]
  J20 = female pin header, 2 pins [form="♀ (female)"]
  J21 = female pin header, 2 pins [form="♀ (female)"]
  J22 = female pin header, 2 pins [form="♀ (female)"]
  J23 = female pin header, 2 pins [form="♀ (female)"]

nets:
  N1: Part2.A0, J18.pin2
  N2: Part2.A1, J18.pin1
  N3: Part2.A2, J19.pin2
  N4: Part2.A3, J19.pin1
  N5: Part2.A4/SDA, J6.pin1, J17.pin2
  N6: Part2.A5/SCL, J6.pin2, J17.pin1
  N7: Part2.D8, J12.pin1
  N8: Part2.D9_PWM, J12.pin2
  N9: Part2.D10_PWM/SS, J11.pin1
  N10: Part2.D11_PWM/MOSI, J11.pin2
  N11: Part2.D12/MISO, J10.pin1
  N12: Part2.D13/SCK, Q3.B, J10.pin2
  GND: Part2.GND, U2.GND, J4.pin1, 12V1.GND, Q3.E, C2.-, J5.pin1, J7.pin1, J22.pin1, J23.pin2
  N13: Part2.AREF, J7.pin2
  N14: Part2.D0/RX, J16.pin1
  N15: Part2.D1/TX, J16.pin2
  N16: Part2.D2, J15.pin1
  N17: Part2.D3_PWM, J15.pin2
  N18: Part2.D4, J14.pin1
  N19: Part2.D5_PWM, J14.pin2
  N20: Part2.D6_PWM, J13.pin1
  N21: Part2.D7, J13.pin2
  N22: Part2.ioref, J20.pin1
  N23: Part2.RESET, J21.pin2
  N24: Part2.3V3, J21.pin1
  5V: Part2.5V, U2.VCC, R3.Pin_1, R4.Pin_1, J22.pin2
  N25: Part2.VIN, J23.pin1
  N26: Part2.N/C, J20.pin2
  N27: U2.RO, R3.Pin_0, CUP_TXD1.pin2
  N28: U2.RE, U2.DE, Q3.C, R4.Pin_0
  N29: U2.DI, CUP_TXD1.pin1
  N30: U2.A, dynamixel1.pin2
  N31: U2.B, dynamixel1.pin1
  N32: J4.pin2, 12V1.VCC, C2.+
